// Logisim project Avila-Nicolas-C1.circ as structural Verilog: 1 circuit, main circuit main
module main (
  input  A,
  input  A_2,
  input  B,
  input  A1,
  input  B1,
  output out_6,
  output out_7,
  output out_8,
  output out_9,
  output out_10,
  output out_11,
  output out_12,
  output out_13,
  output out_14
);

  wire NAND_2_out, NAND_3_out, NAND_4_out, NOR_2_out, NOR_3_out, NOR_4_out;

  not NOT (out_6, A);
  not NAND (out_7, A);  // NAND_Gate
  not NOR (out_8, A);  // NOR_Gate
  and AND (out_9, A_2, B);
  nand NAND_2 (NAND_2_out, A_2, B);
  not NOR_2 (NOR_2_out, A_2);  // NOR_Gate
  not NOR_3 (NOR_3_out, B);  // NOR_Gate
  or OR (out_12, A1, B1);
  not NAND_3 (NAND_3_out, A1);  // NAND_Gate
  not NAND_4 (NAND_4_out, B1);  // NAND_Gate
  nor NOR_4 (NOR_4_out, A1, B1);
  nand NAND_5 (out_10, NAND_2_out, NAND_2_out);
  nor NOR_5 (out_11, NOR_2_out, NOR_3_out);
  nand NAND_6 (out_13, NAND_3_out, NAND_4_out);
  nor NOR_6 (out_14, NOR_4_out, NOR_4_out);

  // Notes on the sheet:
  //   Circuito NOT
  //   Circuito AND
  //   Circuito OR
endmodule
