// Logisim project Avila-Nicolas-taller1.circ as structural Verilog: 2 circuits, main circuit Numeros primos
module Numeros_primos (
  input  A,
  input  B,
  input  C,
  input  D,
  output Numero_primos
);

  wire and_1_out, and_2_out, and_3_out, and_4_out, not_1_out, not_2_out, not_3_out, not_4_out, not_5_out;

  not not_1 (not_1_out, A);
  and and_1 (and_1_out, not_1_out, D);
  not not_2 (not_2_out, A);
  not not_3 (not_3_out, B);
  and and_2 (and_2_out, not_2_out, not_3_out, C);
  not not_4 (not_4_out, B);
  and and_3 (and_3_out, not_4_out, C, D);
  and and_4 (and_4_out, B, not_5_out, D);
  not not_5 (not_5_out, C);
  or or_1 (Numero_primos, and_1_out, and_2_out, and_3_out, and_4_out);
endmodule

module Fibonacci (
  input  A,
  input  B,
  input  C,
  input  D,
  output Fibonacci
);

  wire and_1_out, and_2_out, and_3_out, not_1_out, not_2_out, not_3_out, not_4_out, not_5_out, not_6_out;

  not not_1 (not_1_out, A);
  not not_2 (not_2_out, B);
  not not_3 (not_3_out, B);
  not not_4 (not_4_out, C);
  not not_5 (not_5_out, D);
  not not_6 (not_6_out, C);
  and and_1 (and_1_out, not_1_out, not_2_out);
  and and_2 (and_2_out, not_3_out, not_4_out, not_5_out);
  and and_3 (and_3_out, B, not_6_out, D);
  or or_1 (Fibonacci, and_1_out, and_2_out, and_3_out);
endmodule
