// Logisim project BIN2BCD-NAA.circ as structural Verilog: 2 circuits, main circuit Display
module Display (
  input  D3,
  input  D2,
  input  D1,
  input  D0
);

  wire bin2dec_1_a, bin2dec_1_b, bin2dec_1_c, bin2dec_1_d, bin2dec_1_e, bin2dec_1_f, bin2dec_1_g;

  BIN2DEC bin2dec_1 (
    .D3(D3), .D2(D2), .D1(D1), .D0(D0), .A(bin2dec_1_a), .B(bin2dec_1_b), .C(bin2dec_1_c), .D(bin2dec_1_d),
    .E(bin2dec_1_e), .F(bin2dec_1_f), .G(bin2dec_1_g));
  _7_Segment_Display u_7_segment_display_1 (
    .g(bin2dec_1_g), .f(bin2dec_1_f), .a(bin2dec_1_a), .b(bin2dec_1_b), .e(bin2dec_1_e), .d(bin2dec_1_d),
    .c(bin2dec_1_c));  // open: dp
endmodule

// BIN2BCD-NAA
module BIN2DEC (
  input  D3,
  input  D2,
  input  D1,
  input  D0,
  output A,
  output B,
  output C,
  output D,
  output E,
  output F,
  output G
);

  wire and_1_out, and_2_out, and_3_out, and_4_out, and_5_out, and_6_out, and_7_out, and_8_out, and_9_out,
       and_10_out, and_11_out, and_12_out, and_13_out, and_14_out, and_15_out, and_16_out, not_1_out,
       not_2_out, not_3_out, not_4_out, not_5_out, not_6_out, not_7_out, not_8_out, not_9_out, not_10_out,
       not_11_out, not_12_out, not_13_out, not_14_out, not_15_out, not_16_out, not_17_out, not_18_out,
       not_19_out, not_20_out, not_21_out;

  not not_1 (not_1_out, D2);
  and and_1 (and_1_out, not_1_out, not_2_out);
  not not_2 (not_2_out, D0);
  and and_2 (and_2_out, D2, D0);
  not not_3 (not_3_out, D2);
  not not_4 (not_4_out, D1);
  and and_3 (and_3_out, not_4_out, not_5_out);
  not not_5 (not_5_out, D0);
  and and_4 (and_4_out, D1, D0);
  not not_6 (not_6_out, D1);
  or or_1 (C, not_6_out, D0, D2);
  not not_7 (not_7_out, D2);
  and and_5 (and_5_out, not_7_out, not_8_out);
  not not_8 (not_8_out, D0);
  not not_9 (not_9_out, D2);
  and and_6 (and_6_out, not_9_out, D1);
  and and_7 (and_7_out, D1, not_10_out);
  not not_10 (not_10_out, D0);
  not not_11 (not_11_out, D1);
  and and_8 (and_8_out, D2, not_11_out, D0);
  not not_12 (not_12_out, D2);
  and and_9 (and_9_out, not_12_out, not_13_out);
  not not_13 (not_13_out, D0);
  and and_10 (and_10_out, D1, not_14_out);
  not not_14 (not_14_out, D0);
  not not_15 (not_15_out, D1);
  and and_11 (and_11_out, not_15_out, not_16_out);
  not not_16 (not_16_out, D0);
  and and_12 (and_12_out, D2, not_17_out);
  not not_17 (not_17_out, D1);
  and and_13 (and_13_out, D2, not_18_out);
  not not_18 (not_18_out, D0);
  not not_19 (not_19_out, D2);
  and and_14 (and_14_out, not_19_out, D1);
  and and_15 (and_15_out, D2, not_20_out);
  not not_20 (not_20_out, D1);
  and and_16 (and_16_out, D2, not_21_out);
  not not_21 (not_21_out, D0);
  or or_2 (A, and_1_out, D1, and_2_out, D3);
  or or_3 (B, not_3_out, and_3_out, and_4_out);
  or or_4 (D, and_5_out, and_6_out, and_7_out, and_8_out);
  or or_5 (E, and_9_out, and_10_out);
  or or_6 (F, and_11_out, and_12_out, and_13_out, D3);
  or or_7 (G, and_14_out, and_15_out, and_16_out, D3);
endmodule
