// Logisim project Suma 2 bits.circ as structural Verilog
module Suma_2_bits (
  input  A1,
  input  A0,
  input  B1,
  input  B0,
  output Carry,
  output S1,
  output S0
);

  wire and_1_out, and_2_out, and_3_out, and_4_out, and_5_out, and_6_out, and_7_out, and_8_out, and_9_out,
       and_10_out, not_1_out, not_2_out, not_3_out, not_4_out, not_5_out, not_6_out, not_7_out, not_8_out;

  and and_1 (and_1_out, A0, B1, B0);
  and and_2 (and_2_out, A1, B1);
  and and_3 (and_3_out, A1, A0, B0);
  not not_1 (not_1_out, A1);
  and and_4 (and_4_out, not_1_out, B1);
  not not_2 (not_2_out, A1);
  and and_5 (and_5_out, not_2_out, A0, B0);
  and and_6 (and_6_out, A0, B1, B0);
  and and_7 (and_7_out, A1, not_3_out, not_4_out);
  not not_3 (not_3_out, A0);
  not not_4 (not_4_out, B1);
  not not_5 (not_5_out, B1);
  and and_8 (and_8_out, A1, not_5_out, not_6_out);
  not not_6 (not_6_out, B0);
  not not_7 (not_7_out, A0);
  and and_9 (and_9_out, not_7_out, B0);
  and and_10 (and_10_out, A0, not_8_out);
  not not_8 (not_8_out, B0);
  or or_1 (Carry, and_1_out, and_2_out, and_3_out);
  or or_2 (S1, and_4_out, and_5_out, and_6_out, and_7_out, and_8_out);
  or or_3 (S0, and_9_out, and_10_out);
endmodule
